# Fritzing sketch ADSWheather-NodeMCU_ESQUEMATIC (saved by Fritzing 0.9.3b)
circuit board: 10cm x 8cm
breadboards: 1

parts:
  U1 = ESP8266 NodeMCU LoLin module
  part = BH1750
  PART1 = ML8511 UV Sensor Breakout [part_number=SEN-12705]
  part_2 = BME280 Breakout
  Pluviómetro = RJ11 Jack [package=rj11-6]
  Veleta-Anemo = RJ11 Jack [package=rj11-6]
  part_3 = Adafruit ADS1115 16Bit I2C ADC [part_number="Adafruit #1085"]
  MicroUSB = USB_MICROB_PLUG [package=micro-b-th]
  R3 = Resistor [tolerance=±5% resistance=10k package=THT]  # not connected
  R2 = Resistor [tolerance=±5% resistance=10k package=THT]  # not connected
  R1 = Resistor [tolerance=±5% resistance=10k package=THT]  # not connected
  JP2 = Header 12 [package=1x12_machine-pin-header_lock.004]  # not connected

nets:
  N1: U1.D1, part.SCL, part_2.SCK/SCL, part_3.SCL
  N2: U1.D2, part.SDA, part_2.SDI/SDA, part_3.SDA
  3V3: U1.3V3, part.VCC, PART1.EN, part_2.3.3V, part_3.AIN0, part_3.VDD
  GND: U1.GND, PART1.GND, part_2.GND, Pluviómetro.6, Veleta-Anemo.2, part_3.ADDR, part_3.GND, MicroUSB.GND
  N3: U1.D5, Veleta-Anemo.1
  N4: U1.D6, Pluviómetro.1
  VIN: U1.Vin, MicroUSB.VCC
  N5: U1.A0, Veleta-Anemo.6
  N6: PART1.OUT, part_3.AIN1

notes:
  Veleta
  Anemómetro
  Pluviómetro
  El anemómetro se conecta mediante el RJ-11 a la veleta y de ahí al NodeMCU
  pin 2 - GND
  pin 3 - pin A2 (ADS1115)
  pin 4 - pin D4 (NodeMCU)
  pin 5 - Vdd

custom parts:
  ESP8266 NodeMCU LoLin module: ESP8266 based NodeMCU
  BH1750: Light Sensor
  ML8511 UV Sensor Breakout: Description: The ML8511 breakout is an easy to use ultraviolet light sensor. The MP8511 UV Sensor works by outputing an analog signal in relation to the amount of UV light it detects. This breakout can be very handy in creating devices that warn the user of sunburn or detect the UV index as it relates to weather conditions. This sensor breakout can detect 280-390nm light most effectively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
  Adafruit ADS1115 16Bit I2C ADC: For microcontrollers without an analog-to-digital converter or when you want a higher-precision ADC, the ADS1115 provides 16-bit precision at 860 samples/second over I2C. The chip can be configured as 4 single-ended input channels, or two differential channels. As a nice bonus, it even includes a programmable gain amplifier, up to x16, to help boost up smaller single/differential signals to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
