# Fritzing sketch NodeMCU-Servidor (saved by Fritzing 0.9.3b)
breadboards: 1

parts:
  U2 = LIPO-2000mAh [package=lipo-2000]
  Componente3 = Adafruit ADS1115 16Bit I2C ADC [part_number="Adafruit #1085"]
  Componente4 = BH1750
  PART2 = ML8511 UV Sensor Breakout [part_number=SEN-12705]
  Componente5 = BME280 Breakout
  U3 = ESP8266 NodeMCU LoLin module
  J1 = RJ11 Jack [package=rj11-6]
  R1 = Resistor [tolerance=±5% resistance=10k package="2512 [SMD]"]
  J2 = RJ11 Jack [package=rj11-6]
  R2 = Resistor [tolerance=±5% resistance=10k package="2512 [SMD]"]
  R3 = Resistor [tolerance=±5% resistance=10k package="2512 [SMD]"]

nets:
  VDD: U2.+, Componente3.VDD, Componente4.VCC, Componente5.3.3V, R1.Pin_0
  GND: U2.-, Componente3.ADDR, Componente3.GND, Componente4.GND, Componente4.ADDR, PART2.GND, Componente5.GND, U3.GND, J1.1, J1.2, J2.2
  N1: Componente3.AIN1, PART2.OUT
  N2: Componente3.AIN0, PART2.3.3V
  N3: Componente3.SDA, Componente4.SDA, Componente5.SDI/SDA, U3.D2
  N4: Componente3.SCL, Componente4.SCL, U3.D1
  N5: U3.D5, J1.5, R1.Pin_1
  N6: U3.D6, J2.5, R3.Pin_1
  N7: U3.A0, J1.4, R2.Pin_1

notes:
  D1 - SCK - GPIO 4
  D2 SDI - GPIO 5
  5V
  Anemómetro
  y veleta
  Pines RJ-11
  2 (+Anem)
  3 (+Veleta)
  4 (-Veleta)
  5 (-Anem)
  Pluviómetro

custom parts:
  Adafruit ADS1115 16Bit I2C ADC: For microcontrollers without an analog-to-digital converter or when you want a higher-precision ADC, the ADS1115 provides 16-bit precision at 860 samples/second over I2C. The chip can be configured as 4 single-ended input channels, or two differential channels. As a nice bonus, it even includes a programmable gain amplifier, up to x16, to help boost up smaller single/differential signals to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
  BH1750: Light Sensor
  ML8511 UV Sensor Breakout: Description: The ML8511 breakout is an easy to use ultraviolet light sensor. The MP8511 UV Sensor works by outputing an analog signal in relation to the amount of UV light it detects. This breakout can be very handy in creating devices that warn the user of sunburn or detect the UV index as it relates to weather conditions. This sensor breakout can detect 280-390nm light most effectively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
  ESP8266 NodeMCU LoLin module: ESP8266 based NodeMCU
